# Fritzing sketch wiring (saved by Fritzing 1.0.1rc)
breadboards: 1

parts:
  STM32 = Heltec WiFi LoRa 32 V2 [part_number=HTIT-WB32LA]
  AS5600 = IC, DIP package, 4 pins [chip_label=AS5600]

nets:
  N1: STM32.pin_1, AS5600.pin4
  N2: STM32.pin_16, STM32.pin_17, AS5600.pin1
  N3: STM32.GND, AS5600.pin2
  N4: STM32.pin_21, STM32.pin_22
  N5: STM32.pin_27, AS5600.pin3
